// Logisim project project2.circ as structural Verilog: 5 circuits, main circuit main
module main (
  output [7:0] out_1,
  output [7:0] RegData1,
  output [1:0] ReadReg1,
  output [7:0] RegData2,
  output [1:0] ReadReg2,
  output [1:0] out_6,
  output [7:0] out_7,
  output [7:0] out_8,
  output [7:0] Read_Port
);

  wire and_1_out, and_2_out, and_3_out, and_4_out, CIock_out, clock_1_out, decoder_1_out0, decoder_1_out1,
       decoder_1_out2, decoder_1_out3;
  wire [3:0] multiplexer_1_out, multiplexer_1_out_2;
  wire [7:0] adder_1_out, PC_q, X0_q, X1_q, X2_q, X3_q;

  Register PC (.D(adder_1_out), .clk(CIock_out), .Q(PC_q));  // open: en, clr
  Adder adder_1 (.a(PC_q), .b(8'h1), .out(adder_1_out));  // open: cin, cout
  Clock #(.highDuration(2), .lowDuration(2)) CIock (.out(CIock_out));
  Hex_Digit_Display hex_digit_display_1 (.value(multiplexer_1_out_2));  // open: dp
  Hex_Digit_Display hex_digit_display_2 (.value(multiplexer_1_out));  // open: dp
  Clock clock_1 (.out(clock_1_out));
  RAM ram_1 (.addr(PC_q), .we(1'b0), .oe(1'b1), .clk(CIock_out), .dout(out_1));  // open: din
  RAM #(.addrWidth(4)) ram_2 (
    .addr(out_1[5:2]), .we(1'b0), .oe(1'b1), .clk(clock_1_out), .dout(Read_Port));  // open: din
  Decoder #(.select(2)) decoder_1 (
    .out0(decoder_1_out0), .out1(decoder_1_out1), .out2(decoder_1_out2), .out3(decoder_1_out3),
    .sel(out_1[1:0]));  // open: en
  Multiplexer #(.select(2), .width(8)) multiplexer_1 (
    .in0(Read_Port), .in1(out_7), .in2(out_8), .out({multiplexer_1_out_2, multiplexer_1_out}),
    .sel(out_1[7:6]));  // open: in3
  Adder adder_2 (.a(RegData1), .b(RegData2), .out(out_7));  // open: cin, cout
  Subtractor subtractor_1 (.a(RegData1), .b(RegData2), .out(out_8));  // open: bin, bout
  and and_1 (and_1_out, 1'b1, decoder_1_out0);
  and and_2 (and_2_out, 1'b1, decoder_1_out1);
  and and_3 (and_3_out, 1'b1, decoder_1_out2);
  and and_4 (and_4_out, 1'b1, decoder_1_out3);
  Register X0 (.D({multiplexer_1_out_2, multiplexer_1_out}), .en(and_1_out), .clk(CIock_out), .Q(X0_q));  // open: clr
  Register X1 (.D({multiplexer_1_out_2, multiplexer_1_out}), .en(and_2_out), .clk(CIock_out), .Q(X1_q));  // open: clr
  Register X2 (.D({multiplexer_1_out_2, multiplexer_1_out}), .en(and_3_out), .clk(CIock_out), .Q(X2_q));  // open: clr
  Register X3 (.D({multiplexer_1_out_2, multiplexer_1_out}), .en(and_4_out), .clk(CIock_out), .Q(X3_q));  // open: clr
  Multiplexer #(.select(2), .width(8)) multiplexer_2 (
    .in0(X0_q), .in1(X1_q), .in2(X2_q), .in3(X3_q), .out(RegData1), .sel(out_1[5:4]));
  Multiplexer #(.select(2), .width(8)) multiplexer_3 (
    .in0(X0_q), .in1(X1_q), .in2(X2_q), .in3(X3_q), .out(RegData2), .sel(out_1[3:2]));

  assign out_6 = out_1[7:6];
  assign ReadReg1 = out_1[5:4];
  assign ReadReg2 = out_1[3:2];

  // Notes on the sheet:
  //   ONPAR CPU
  //   Zack Rimshnick
  //   Dominick Battinelli
  //   ALU
  //   I pledge my honor that I have abided by the Stevens Honor System.
  //   ADDER
  //   SUBBER
  //   RegWrite
  //   RegDataW
  //   INSTRUCTION MEMORY
  //   WriteReg
  //   Data Memory
  //   REGISTER FILE
  //   RegData2
  //   RegData2
  //   RegData1
  //   RegData1
endmodule

module memory (
  output [7:0] Read_Port
);

  wire CIock_out;
  wire [7:0] adder_1_out, PC_q;

  Register PC (.D(adder_1_out), .clk(CIock_out), .Q(PC_q));  // open: en, clr
  Adder adder_1 (.a(PC_q), .b(8'h1), .out(adder_1_out));  // open: cin, cout
  Clock CIock (.out(CIock_out));
  RAM ram_1 (.addr(PC_q), .we(1'b0), .oe(1'b1), .clk(CIock_out), .dout(Read_Port));  // open: din
endmodule

module register_file (
  input  [1:0] WriteReg,
  input  [1:0] ReadReg1,
  input  [7:0] RegDataW,
  input  [1:0] ReadReg2,
  input  RegWrite,
  output [7:0] RegData1,
  output [7:0] RegData2
);

  wire and_1_out, and_2_out, and_3_out, and_4_out, CIock_out, decoder_1_out0, decoder_1_out1, decoder_1_out2,
       decoder_1_out3;
  wire [7:0] X0_q, X1_q, X2_q, X3_q;

  Clock CIock (.out(CIock_out));
  Decoder #(.select(2)) decoder_1 (
    .out0(decoder_1_out0), .out1(decoder_1_out1), .out2(decoder_1_out2), .out3(decoder_1_out3), .sel(WriteReg));  // open: en
  and and_1 (and_1_out, RegWrite, decoder_1_out0);
  and and_2 (and_2_out, RegWrite, decoder_1_out1);
  and and_3 (and_3_out, RegWrite, decoder_1_out2);
  and and_4 (and_4_out, RegWrite, decoder_1_out3);
  Register X0 (.D(RegDataW), .en(and_1_out), .clk(CIock_out), .Q(X0_q));  // open: clr
  Register X1 (.D(RegDataW), .en(and_2_out), .clk(CIock_out), .Q(X1_q));  // open: clr
  Register X2 (.D(RegDataW), .en(and_3_out), .clk(CIock_out), .Q(X2_q));  // open: clr
  Register X3 (.D(RegDataW), .en(and_4_out), .clk(CIock_out), .Q(X3_q));  // open: clr
  Multiplexer #(.select(2), .width(8)) multiplexer_1 (
    .in0(X0_q), .in1(X1_q), .in2(X2_q), .in3(X3_q), .out(RegData1), .sel(ReadReg1));
  Multiplexer #(.select(2), .width(8)) multiplexer_2 (
    .in0(X0_q), .in1(X1_q), .in2(X2_q), .in3(X3_q), .out(RegData2), .sel(ReadReg2));
endmodule

module multiplexor (
  input  Switch,
  input  [3:0] inputA,
  input  [3:0] inputB,
  output [3:0] AorB
);

  wire and_1_out, and_2_out, and_3_out, and_4_out, and_5_out, and_6_out, and_7_out, and_8_out, not_1_out;

  not not_1 (not_1_out, Switch);
  and and_1 (and_1_out, not_1_out, inputA[0]);
  and and_2 (and_2_out, Switch, inputB[0]);
  and and_3 (and_3_out, not_1_out, inputA[1]);
  and and_4 (and_4_out, Switch, inputB[1]);
  and and_5 (and_5_out, not_1_out, inputA[2]);
  and and_6 (and_6_out, Switch, inputB[2]);
  and and_7 (and_7_out, not_1_out, inputA[3]);
  and and_8 (and_8_out, Switch, inputB[3]);
  or or_1 (AorB[0], and_1_out, and_2_out);
  or or_2 (AorB[1], and_3_out, and_4_out);
  or or_3 (AorB[2], and_5_out, and_6_out);
  or or_4 (AorB[3], and_7_out, and_8_out);

  // Notes on the sheet:
  //   Least sig. bit
  //   Bit 1
  //   Bit 2
  //   Most sig. Bit
endmodule

module nib_adder (
  input  cin,
  input  [3:0] inputA,
  input  [3:0] inputB,
  output [3:0] AplusB,
  output Cflag
);

  wire and_1_out, and_2_out, and_3_out, and_4_out, and_5_out, and_6_out, and_7_out, and_8_out, and_9_out,
       and_10_out, and_11_out, and_12_out, or_1_out, or_2_out, or_3_out, xor_1_out, xor_2_out, xor_3_out,
       xor_4_out;

  and and_1 (and_1_out, or_3_out, inputB[3]);
  and and_2 (and_2_out, or_3_out, inputA[3]);
  and and_3 (and_3_out, inputA[3], inputB[3]);
  xor xor_1 (xor_1_out, cin, inputA[0]);
  and and_4 (and_4_out, cin, inputB[0]);
  and and_5 (and_5_out, cin, inputA[0]);
  and and_6 (and_6_out, inputA[0], inputB[0]);
  xor xor_2 (xor_2_out, or_1_out, inputA[1]);
  and and_7 (and_7_out, or_1_out, inputB[1]);
  and and_8 (and_8_out, or_1_out, inputA[1]);
  and and_9 (and_9_out, inputA[1], inputB[1]);
  xor xor_3 (xor_3_out, or_2_out, inputA[2]);
  and and_10 (and_10_out, or_2_out, inputB[2]);
  and and_11 (and_11_out, or_2_out, inputA[2]);
  and and_12 (and_12_out, inputA[2], inputB[2]);
  xor xor_4 (xor_4_out, or_3_out, inputA[3]);
  xor xor_5 (AplusB[0], xor_1_out, inputB[0]);
  xor xor_6 (AplusB[1], xor_2_out, inputB[1]);
  xor xor_7 (AplusB[2], xor_3_out, inputB[2]);
  xor xor_8 (AplusB[3], xor_4_out, inputB[3]);
  or or_1 (or_1_out, and_4_out, and_5_out, and_6_out);
  or or_2 (or_2_out, and_7_out, and_8_out, and_9_out);
  or or_3 (or_3_out, and_10_out, and_11_out, and_12_out);
  or or_4 (Cflag, and_1_out, and_2_out, and_3_out);

  // Notes on the sheet:
  //   Least Sig. Bit
  //   Bit 1
  //   Bit 2
  //   Most Sig. Bit
  //   Zack Rimshnick
endmodule
